// Logisim project (A+B).(A`+B`).circ as structural Verilog: 1 circuit, main circuit main
module main (
  input  A,
  input  B,
  output out_3
);

  wire not_1_out, not_2_out, or_1_out, or_2_out;

  not not_1 (not_1_out, B);
  not not_2 (not_2_out, A);
  or or_1 (or_1_out, A, B);
  or or_2 (or_2_out, not_1_out, not_2_out);
  and and_1 (out_3, or_1_out, or_2_out);
endmodule
