// Logisim project Logic Circuit.circ as structural Verilog: 1 circuit, main circuit main
module main (
  input  S_0,
  input  D_0,
  input  D_1,
  input  S_1,
  input  D_2,
  input  D_3,
  input  S_2,
  input  D_4,
  input  D_5,
  input  D_6,
  input  D_7,
  output out_12
);

  wire and_1_out, and_2_out, and_3_out, and_4_out, and_5_out, and_6_out, and_7_out, and_8_out, not_1_out,
       not_2_out, not_3_out, not_4_out, not_5_out, not_6_out, not_7_out, not_8_out, not_9_out, not_10_out,
       not_11_out, not_12_out;

  not not_1 (not_1_out, S_2);
  not not_2 (not_2_out, S_0);
  not not_3 (not_3_out, S_1);
  not not_4 (not_4_out, S_2);
  not not_5 (not_5_out, S_1);
  not not_6 (not_6_out, S_2);
  not not_7 (not_7_out, S_0);
  not not_8 (not_8_out, S_2);
  not not_9 (not_9_out, S_0);
  not not_10 (not_10_out, S_1);
  not not_11 (not_11_out, S_1);
  not not_12 (not_12_out, S_0);
  and and_1 (and_1_out, not_2_out, not_3_out, not_4_out, D_0);
  and and_2 (and_2_out, not_5_out, not_6_out, S_0, D_1);
  and and_3 (and_3_out, not_7_out, not_1_out, S_1, D_2);
  and and_4 (and_4_out, S_1, S_0, not_8_out, D_3);
  and and_5 (and_5_out, not_9_out, not_10_out, S_2, D_4);
  and and_6 (and_6_out, S_0, not_11_out, S_2, D_5);
  and and_7 (and_7_out, not_12_out, S_1, S_2, D_6);
  and and_8 (and_8_out, S_2, S_1, S_0, D_7);
  or or_1 (out_12, and_1_out, and_2_out, and_3_out, and_4_out, and_5_out, and_6_out, and_7_out, and_8_out);
endmodule
