// Logisim project Question CS191092 2B Poorab gangwani DLD.circ as structural Verilog: 1 circuit, main circuit main
module main (
  input  A,
  input  B,
  input  C,
  input  in_4,
  input  in_5,
  output Z1,
  output Z1_2
);

  wire and_1_out, and_2_out, and_3_out, and_4_out, and_5_out, and_6_out, and_7_out, and_8_out, and_9_out,
       and_10_out, not_1_out, not_2_out, not_3_out, not_4_out, not_5_out, or_1_out;

  not not_1 (not_1_out, B);
  not not_2 (not_2_out, C);
  not not_3 (not_3_out, C);
  and and_1 (and_1_out, A, not_1_out, not_2_out);
  and and_2 (and_2_out, A, not_1_out, C);
  and and_3 (and_3_out, A, B, not_3_out);
  and and_4 (and_4_out, B, A, C);
  or or_1 (or_1_out, and_1_out, and_2_out, and_3_out, and_4_out);
  and and_5 (and_5_out, B, or_1_out);
  and and_6 (and_6_out, or_1_out, C);
  not not_4 (not_4_out, or_1_out);
  not not_5 (not_5_out, or_1_out);
  and and_7 (and_7_out, in_4, not_4_out);
  and and_8 (and_8_out, in_5, not_5_out);
  xor XOR (Z1, and_5_out, and_6_out);
  and and_9 (and_9_out, and_7_out, B);
  and and_10 (and_10_out, and_8_out, C);
  and and_11 (Z1_2, and_9_out, and_10_out);
endmodule
