// Logisim project half header using or ,and, not.circ as structural Verilog: 1 circuit, main circuit main
module main (
  input  A,
  input  B,
  output out_3
);

  wire and_1_out, and_2_out, and_3_out, not_1_out, not_2_out, or_1_out;

  not not_1 (not_1_out, A);
  not not_2 (not_2_out, B);
  and and_1 (and_1_out, not_1_out, B);
  and and_2 (and_2_out, not_2_out, A);
  and and_3 (and_3_out, A, B);
  or or_1 (or_1_out, and_1_out, and_2_out);
  or or_2 (out_3, or_1_out, and_3_out);
endmodule
